# Fritzing sketch hydroponic_circuit (saved by Fritzing 0.9.3b)

parts:
  Part2 = USB Type A Female Breakout Board [part_number=BOB-12700]
  Mosfet_driver_module1 = IFR520 MOS module [package=THT]
  Part3 = Adafruit Micro USB Breakout [part_number="Adafruit #1833"]
  Parte2 = FC-28 Soil Hygrometer Module
  Parte3 = FC-28 Soil Hygrometer Module - Probe
  Part9 = Adafruit Metro Mini [part_number="Adafruit #2590"]
  Parte4 = FC-28 Soil Hygrometer Module
  Parte5 = FC-28 Soil Hygrometer Module - Probe
  Part10 = Adafruit Metro Mini [part_number="Adafruit #2590"]
  Part4 = Soil Moisture Sensor
  Part1 = Adafruit Metro Mini [part_number="Adafruit #2590"]
  Part11 = USB Type A Female Breakout Board [part_number=BOB-12700]
  Mosfet_driver_module2 = IFR520 MOS module [package=THT]
  Part12 = Adafruit Micro USB Breakout [part_number="Adafruit #1833"]

nets:
  N1: Part2.VCC, Mosfet_driver_module1.pin4
  N2: Part2.GND, Mosfet_driver_module1.pin5
  N3: Mosfet_driver_module1.pin1, Part1.AD1
  N4: Mosfet_driver_module1.pin2, Part1.+5V
  GND: Mosfet_driver_module1.pin3, Part4.GND, Part1.GND
  N5: Mosfet_driver_module1.pin6, Part3.VBUS
  N6: Mosfet_driver_module1.pin7, Part3.GND
  VCC: Parte2.VCC, Part9.3.3V
  GND_2: Parte2.GND, Part9.GND
  N7: Parte2.AO, Part9.AD0
  N8: Parte2.POS, Parte3.POS
  N9: Parte2.NEG, Parte3.NEG
  VCC_2: Parte4.VCC, Part10.3.3V
  GND_3: Parte4.GND, Part10.GND, Mosfet_driver_module2.pin3
  N10: Parte4.AO, Part10.AD0
  N11: Parte4.POS, Parte5.POS
  N12: Parte4.NEG, Parte5.NEG
  N13: Part10.AD1, Mosfet_driver_module2.pin1
  N14: Part10.+5V, Mosfet_driver_module2.pin2
  N15: Part4.SIG, Part1.AD0
  VCC_3: Part4.VCC, Part1.3.3V
  N16: Part11.VCC, Mosfet_driver_module2.pin4
  N17: Part11.GND, Mosfet_driver_module2.pin5
  N18: Mosfet_driver_module2.pin6, Part12.VBUS
  N19: Mosfet_driver_module2.pin7, Part12.GND

notes:
  Part 1
  Complete Circuit
  Using onboard moisture sensor

custom parts:
  USB Type A Female Breakout Board: USB breakout board for a Type A connector. sparkfun.com
  IFR520 MOS module: Breakout board for the IFR520 MOSFET transistor. The module is designed to switch heavy DC loads from a single digital pin of your microcontroller. Its main purpose is to provide a low cost way to drive a DC motor for robotics applications, but the module can be used to control most high current DC loads. Screw terminals are provided to interface to your load and external power source. An LED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
  Adafruit Micro USB Breakout: Simple but effective - this breakout board has a USB Micro-B connector, with all 5 pins broken out. Great for pairing with a microcontroller with USB support, or adding USB 5V power to a project. We use a micro-AB connector with through-hole shielding pads for an excellent strong connection - it won't rip off by accident! Comes with one fully assembled and tested micro B breakout PCB and a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
  FC-28 Soil Hygrometer Module: The FC-28 is a soil hygrometer module that uses the Texas Instruments LM393 comparator chip to provide an analog measurement of soil humidity. The digital output is high when soil moisture is over a certain threshold, as determined by adjusting the potentiometer.
  FC-28 Soil Hygrometer Module - Probe: The FC-28 is a soil hygrometer module that uses the Texas Instruments LM393 comparator chip to provide an analog measurement of soil humidity.
  Adafruit Metro Mini: We sure love the ATmega328 here at Adafruit, and we use them a lot for our own projects. The processor has plenty of GPIO, Analog inputs, hardware UART SPI and I2C, timers and PWM galore - just enough for most simple projects. When we need to go small, we use a Pro Trinket 3V or 5V, but if you want to have USB-to-Serial built in, we reach for an Adafruit METRO Mini. METRO Mini is the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
